// Logisim project 32bit_riscv_cpu.circ as structural Verilog: 3 circuits, main circuit main
module register_file (
  input  [4:0] rd_in,
  input  clock,
  input  clear,
  input  [31:0] data_in,
  input  [4:0] rs1_in,
  input  [4:0] rs2_in,
  output [31:0] rs1,
  output [31:0] rs2
);

  wire [2:0] demultiplexer_1_out1;
  wire [3:0] demultiplexer_1_out4, demultiplexer_1_out8, demultiplexer_1_out12, demultiplexer_1_out16,
       demultiplexer_1_out20, demultiplexer_1_out24, demultiplexer_1_out28;
  wire [31:0] reg01_q, reg02_q, reg03_q, reg04_q, reg05_q, reg06_q, reg07_q, reg08_q, reg09_q, reg10_q,
       reg11_q, reg12_q, reg13_q, reg14_q, reg15_q, reg16_q, reg17_q, reg18_q, reg19_q, reg20_q, reg21_q,
       reg22_q, reg23_q, reg24_q, reg25_q, reg26_q, reg27_q, reg28_q, reg29_q, reg30_q, reg31_q;

  Register #(.width(32)) reg01 (.D(data_in), .en(demultiplexer_1_out1[0]), .clk(clock), .Q(reg01_q), .clr(clear));
  Register #(.width(32)) reg02 (.D(data_in), .en(demultiplexer_1_out1[1]), .clk(clock), .Q(reg02_q), .clr(clear));
  Register #(.width(32)) reg03 (.D(data_in), .en(demultiplexer_1_out1[2]), .clk(clock), .Q(reg03_q), .clr(clear));
  Register #(.width(32)) reg16 (.D(data_in), .en(demultiplexer_1_out16[0]), .clk(clock), .Q(reg16_q), .clr(clear));
  Register #(.width(32)) reg17 (.D(data_in), .en(demultiplexer_1_out16[1]), .clk(clock), .Q(reg17_q), .clr(clear));
  Register #(.width(32)) reg18 (.D(data_in), .en(demultiplexer_1_out16[2]), .clk(clock), .Q(reg18_q), .clr(clear));
  Register #(.width(32)) reg19 (.D(data_in), .en(demultiplexer_1_out16[3]), .clk(clock), .Q(reg19_q), .clr(clear));
  Demultiplexer #(.select(5)) demultiplexer_1 (
    .out1(demultiplexer_1_out1[0]), .out2(demultiplexer_1_out1[1]), .out3(demultiplexer_1_out1[2]),
    .out4(demultiplexer_1_out4[0]), .out5(demultiplexer_1_out4[1]), .out6(demultiplexer_1_out4[2]),
    .out7(demultiplexer_1_out4[3]), .out8(demultiplexer_1_out8[0]), .out9(demultiplexer_1_out8[1]),
    .out10(demultiplexer_1_out8[2]), .out11(demultiplexer_1_out8[3]), .out12(demultiplexer_1_out12[0]),
    .out13(demultiplexer_1_out12[1]), .out14(demultiplexer_1_out12[2]), .out15(demultiplexer_1_out12[3]),
    .out16(demultiplexer_1_out16[0]), .out17(demultiplexer_1_out16[1]), .out18(demultiplexer_1_out16[2]),
    .out19(demultiplexer_1_out16[3]), .out20(demultiplexer_1_out20[0]), .out21(demultiplexer_1_out20[1]),
    .out22(demultiplexer_1_out20[2]), .out23(demultiplexer_1_out20[3]), .out24(demultiplexer_1_out24[0]),
    .out25(demultiplexer_1_out24[1]), .out26(demultiplexer_1_out24[2]), .out27(demultiplexer_1_out24[3]),
    .out28(demultiplexer_1_out28[0]), .out29(demultiplexer_1_out28[1]), .out30(demultiplexer_1_out28[2]),
    .out31(demultiplexer_1_out28[3]), .sel(rd_in));  // open: out0, in
  Register #(.width(32)) reg04 (.D(data_in), .en(demultiplexer_1_out4[0]), .clk(clock), .Q(reg04_q), .clr(clear));
  Register #(.width(32)) reg05 (.D(data_in), .en(demultiplexer_1_out4[1]), .clk(clock), .Q(reg05_q), .clr(clear));
  Register #(.width(32)) reg06 (.D(data_in), .en(demultiplexer_1_out4[2]), .clk(clock), .Q(reg06_q), .clr(clear));
  Register #(.width(32)) reg07 (.D(data_in), .en(demultiplexer_1_out4[3]), .clk(clock), .Q(reg07_q), .clr(clear));
  Register #(.width(32)) reg20 (.D(data_in), .en(demultiplexer_1_out20[0]), .clk(clock), .Q(reg20_q), .clr(clear));
  Register #(.width(32)) reg21 (.D(data_in), .en(demultiplexer_1_out20[1]), .clk(clock), .Q(reg21_q), .clr(clear));
  Register #(.width(32)) reg22 (.D(data_in), .en(demultiplexer_1_out20[2]), .clk(clock), .Q(reg22_q), .clr(clear));
  Register #(.width(32)) reg23 (.D(data_in), .en(demultiplexer_1_out20[3]), .clk(clock), .Q(reg23_q), .clr(clear));
  Register #(.width(32)) reg08 (.D(data_in), .en(demultiplexer_1_out8[0]), .clk(clock), .Q(reg08_q), .clr(clear));
  Register #(.width(32)) reg09 (.D(data_in), .en(demultiplexer_1_out8[1]), .clk(clock), .Q(reg09_q), .clr(clear));
  Register #(.width(32)) reg10 (.D(data_in), .en(demultiplexer_1_out8[2]), .clk(clock), .Q(reg10_q), .clr(clear));
  Register #(.width(32)) reg11 (.D(data_in), .en(demultiplexer_1_out8[3]), .clk(clock), .Q(reg11_q), .clr(clear));
  Register #(.width(32)) reg24 (.D(data_in), .en(demultiplexer_1_out24[0]), .clk(clock), .Q(reg24_q), .clr(clear));
  Register #(.width(32)) reg25 (.D(data_in), .en(demultiplexer_1_out24[1]), .clk(clock), .Q(reg25_q), .clr(clear));
  Register #(.width(32)) reg26 (.D(data_in), .en(demultiplexer_1_out24[2]), .clk(clock), .Q(reg26_q), .clr(clear));
  Register #(.width(32)) reg27 (.D(data_in), .en(demultiplexer_1_out24[3]), .clk(clock), .Q(reg27_q), .clr(clear));
  Multiplexer #(.select(5), .width(32)) multiplexer_1 (
    .in0({32{1'b0}}), .in1(reg01_q), .in2(reg02_q), .in3(reg03_q), .in4(reg04_q), .in5(reg05_q),
    .in6(reg06_q), .in7(reg07_q), .in8(reg08_q), .in9(reg09_q), .in10(reg10_q), .in11(reg11_q),
    .in12(reg12_q), .in13(reg13_q), .in14(reg14_q), .in15(reg15_q), .in16(reg16_q), .in17(reg17_q),
    .in18(reg18_q), .in19(reg19_q), .in20(reg20_q), .in21(reg21_q), .in22(reg22_q), .in23(reg23_q),
    .in24(reg24_q), .in25(reg25_q), .in26(reg26_q), .in27(reg27_q), .in28(reg28_q), .in29(reg29_q),
    .in30(reg30_q), .in31(reg31_q), .out(rs2), .sel(rs2_in));
  Register #(.width(32)) reg12 (.D(data_in), .en(demultiplexer_1_out12[0]), .clk(clock), .Q(reg12_q), .clr(clear));
  Register #(.width(32)) reg13 (.D(data_in), .en(demultiplexer_1_out12[1]), .clk(clock), .Q(reg13_q), .clr(clear));
  Register #(.width(32)) reg14 (.D(data_in), .en(demultiplexer_1_out12[2]), .clk(clock), .Q(reg14_q), .clr(clear));
  Register #(.width(32)) reg15 (.D(data_in), .en(demultiplexer_1_out12[3]), .clk(clock), .Q(reg15_q), .clr(clear));
  Register #(.width(32)) reg28 (.D(data_in), .en(demultiplexer_1_out28[0]), .clk(clock), .Q(reg28_q), .clr(clear));
  Register #(.width(32)) reg29 (.D(data_in), .en(demultiplexer_1_out28[1]), .clk(clock), .Q(reg29_q), .clr(clear));
  Register #(.width(32)) reg30 (.D(data_in), .en(demultiplexer_1_out28[2]), .clk(clock), .Q(reg30_q), .clr(clear));
  Register #(.width(32)) reg31 (.D(data_in), .en(demultiplexer_1_out28[3]), .clk(clock), .Q(reg31_q), .clr(clear));
  Multiplexer #(.select(5), .width(32)) multiplexer_2 (
    .in0({32{1'b0}}), .in1(reg01_q), .in2(reg02_q), .in3(reg03_q), .in4(reg04_q), .in5(reg05_q),
    .in6(reg06_q), .in7(reg07_q), .in8(reg08_q), .in9(reg09_q), .in10(reg10_q), .in11(reg11_q),
    .in12(reg12_q), .in13(reg13_q), .in14(reg14_q), .in15(reg15_q), .in16(reg16_q), .in17(reg17_q),
    .in18(reg18_q), .in19(reg19_q), .in20(reg20_q), .in21(reg21_q), .in22(reg22_q), .in23(reg23_q),
    .in24(reg24_q), .in25(reg25_q), .in26(reg26_q), .in27(reg27_q), .in28(reg28_q), .in29(reg29_q),
    .in30(reg30_q), .in31(reg31_q), .out(rs1), .sel(rs1_in));
endmodule

module alu (
  input  [6:0] opcode,
  input  [31:0] rs2,
  input  [31:0] rs1,
  input  [6:0] funct7,
  input  [23:0] ram,
  input  [2:0] funct3,
  input  [24:0] imm,
  output [31:0] alu_out
);

  wire comparator_1_lt, comparator_2_lt, comparator_3_eq, comparator_4_eq, comparator_5_lt, comparator_6_lt,
       comparator_7_eq, comparator_8_eq;
  wire [7:0] rom_1_data;
  wire [31:0] adder_1_out, adder_2_out, and_1_out, and_2_out, bit_extender_1_out, bit_extender_2_out,
       bit_extender_3_out, bit_extender_4_out, bit_extender_5_out, bit_extender_6_out, bit_extender_7_out,
       bit_extender_8_out, bit_extender_9_out, bit_extender_10_out, controlled_buffer_2_out,
       controlled_buffer_10_out, controlled_buffer_20_out, multiplexer_1_out, multiplexer_2_out,
       multiplexer_3_out, or_1_out, or_2_out, shifter_1_out, shifter_2_out, shifter_3_out, shifter_4_out,
       shifter_5_out, shifter_6_out, subtractor_1_out, xor_1_out, xor_2_out;

  ROM #(.addrWidth(3)) rom_1 (.addr(funct3), .data(rom_1_data));
  Shifter #(.shift("lr"), .width(32)) shifter_1 (.in(rs1), .\dist (rs2[4:0]), .out(shifter_1_out));
  Shifter #(.shift("ar"), .width(32)) shifter_2 (.in(rs1), .\dist (rs2[4:0]), .out(shifter_2_out));
  Comparator #(.mode("unsigned"), .width(32)) comparator_1 (.a(rs1), .b(rs2), .lt(comparator_1_lt));  // open: gt, eq
  Comparator #(.width(32)) comparator_2 (.a(rs1), .b(rs2), .lt(comparator_2_lt));  // open: gt, eq
  Subtractor #(.width(32)) subtractor_1 (.a(rs1), .b(rs2), .out(subtractor_1_out));  // open: bin, bout
  Adder #(.width(32)) adder_1 (.a(rs1), .b(rs2), .out(adder_1_out));  // open: cin, cout
  Comparator #(.width(7)) comparator_3 (.a(funct7), .b(7'b0100000), .eq(comparator_3_eq));  // open: gt, lt
  assign and_1_out = rs1 & rs2;  // AND_Gate and_1, 32 bits wide
  assign or_1_out = rs1 | rs2;  // OR_Gate or_1, 32 bits wide
  Multiplexer #(.width(32)) multiplexer_1 (
    .in0(shifter_1_out), .in1(shifter_2_out), .out(multiplexer_1_out), .sel(comparator_3_eq));
  assign xor_1_out = rs1 ^ rs2;  // XOR_Gate xor_1, 32 bits wide
  assign bit_extender_1_out = {{31{1'b0}}, comparator_1_lt};  // Bit_Extender bit_extender_1
  assign bit_extender_2_out = {{31{1'b0}}, comparator_2_lt};  // Bit_Extender bit_extender_2
  Shifter #(.width(32)) shifter_3 (.in(rs1), .\dist (rs2[4:0]), .out(shifter_3_out));
  Multiplexer #(.width(32)) multiplexer_2 (
    .in0(subtractor_1_out), .in1(adder_1_out), .out(multiplexer_2_out), .sel(comparator_3_eq));
  assign alu_out = comparator_4_eq ? controlled_buffer_2_out : 32'bz;  // Controlled_Buffer controlled_buffer_1
  Comparator #(.width(7)) comparator_4 (.a(opcode), .b(7'b0110011), .eq(comparator_4_eq));  // open: gt, lt
  assign controlled_buffer_2_out = rom_1_data[7] ? and_1_out : 32'bz;  // Controlled_Buffer controlled_buffer_2
  assign controlled_buffer_2_out = rom_1_data[6] ? or_1_out : 32'bz;  // Controlled_Buffer controlled_buffer_3
  assign controlled_buffer_2_out = rom_1_data[5] ? multiplexer_1_out : 32'bz;  // Controlled_Buffer controlled_buffer_4
  assign controlled_buffer_2_out = rom_1_data[4] ? xor_1_out : 32'bz;  // Controlled_Buffer controlled_buffer_5
  assign controlled_buffer_2_out = rom_1_data[3] ? bit_extender_1_out : 32'bz;  // Controlled_Buffer controlled_buffer_6
  assign controlled_buffer_2_out = rom_1_data[2] ? bit_extender_2_out : 32'bz;  // Controlled_Buffer controlled_buffer_7
  assign controlled_buffer_2_out = rom_1_data[1] ? shifter_3_out : 32'bz;  // Controlled_Buffer controlled_buffer_8
  assign controlled_buffer_2_out = rom_1_data[0] ? multiplexer_2_out : 32'bz;  // Controlled_Buffer controlled_buffer_9
  assign bit_extender_3_out = {{20{imm[11]}}, imm[11:0]};  // Bit_Extender bit_extender_3
  Shifter #(.shift("lr"), .width(32)) shifter_4 (.in(rs1), .\dist (imm[4:0]), .out(shifter_4_out));
  Shifter #(.shift("ar"), .width(32)) shifter_5 (.in(rs1), .\dist (imm[4:0]), .out(shifter_5_out));
  Comparator #(.mode("unsigned"), .width(32)) comparator_5 (
    .a(rs1), .b(bit_extender_3_out), .lt(comparator_5_lt));  // open: gt, eq
  Comparator #(.width(32)) comparator_6 (.a(rs1), .b(bit_extender_3_out), .lt(comparator_6_lt));  // open: gt, eq
  assign and_2_out = rs1 & bit_extender_3_out;  // AND_Gate and_2, 32 bits wide
  assign or_2_out = rs1 | bit_extender_3_out;  // OR_Gate or_2, 32 bits wide
  Multiplexer #(.width(32)) multiplexer_3 (
    .in0(shifter_4_out), .in1(shifter_5_out), .out(multiplexer_3_out), .sel(comparator_3_eq));
  assign xor_2_out = rs1 ^ bit_extender_3_out;  // XOR_Gate xor_2, 32 bits wide
  assign bit_extender_4_out = {{31{comparator_5_lt}}, comparator_5_lt};  // Bit_Extender bit_extender_4
  assign bit_extender_5_out = {{31{comparator_6_lt}}, comparator_6_lt};  // Bit_Extender bit_extender_5
  Shifter #(.width(32)) shifter_6 (.in(rs1), .\dist (imm[4:0]), .out(shifter_6_out));
  Adder #(.width(32)) adder_2 (.a(rs1), .b(bit_extender_3_out), .out(adder_2_out));  // open: cin, cout
  Comparator #(.width(7)) comparator_7 (.a(opcode), .b(7'b0010011), .eq(comparator_7_eq));  // open: gt, lt
  assign controlled_buffer_10_out = rom_1_data[7] ? and_2_out : 32'bz;  // Controlled_Buffer controlled_buffer_10
  assign controlled_buffer_10_out = rom_1_data[6] ? or_2_out : 32'bz;  // Controlled_Buffer controlled_buffer_11
  assign controlled_buffer_10_out = rom_1_data[5] ? multiplexer_3_out : 32'bz;  // Controlled_Buffer controlled_buffer_12
  assign controlled_buffer_10_out = rom_1_data[4] ? xor_2_out : 32'bz;  // Controlled_Buffer controlled_buffer_13
  assign controlled_buffer_10_out = rom_1_data[3] ? bit_extender_4_out : 32'bz;  // Controlled_Buffer controlled_buffer_14
  assign controlled_buffer_10_out = rom_1_data[2] ? bit_extender_5_out : 32'bz;  // Controlled_Buffer controlled_buffer_15
  assign controlled_buffer_10_out = rom_1_data[1] ? shifter_6_out : 32'bz;  // Controlled_Buffer controlled_buffer_16
  assign controlled_buffer_10_out = rom_1_data[0] ? adder_2_out : 32'bz;  // Controlled_Buffer controlled_buffer_17
  assign alu_out = comparator_7_eq ? controlled_buffer_10_out : 32'bz;  // Controlled_Buffer controlled_buffer_18
  assign bit_extender_6_out = {{16{1'b0}}, ram[15:0]};  // Bit_Extender bit_extender_6
  assign bit_extender_7_out = {{24{1'b0}}, ram[7:0]};  // Bit_Extender bit_extender_7
  assign bit_extender_8_out = {{8{ram[23]}}, ram};  // Bit_Extender bit_extender_8
  assign bit_extender_9_out = {{16{ram[15]}}, ram[15:0]};  // Bit_Extender bit_extender_9
  assign bit_extender_10_out = {{24{ram[7]}}, ram[7:0]};  // Bit_Extender bit_extender_10
  assign alu_out = comparator_8_eq ? controlled_buffer_20_out : 32'bz;  // Controlled_Buffer controlled_buffer_19
  Comparator #(.width(7)) comparator_8 (.a(opcode), .b(7'b0000011), .eq(comparator_8_eq));  // open: gt, lt
  assign controlled_buffer_20_out = rom_1_data[5] ? bit_extender_6_out : 32'bz;  // Controlled_Buffer controlled_buffer_20
  assign controlled_buffer_20_out = rom_1_data[4] ? bit_extender_7_out : 32'bz;  // Controlled_Buffer controlled_buffer_21
  assign controlled_buffer_20_out = rom_1_data[2] ? bit_extender_8_out : 32'bz;  // Controlled_Buffer controlled_buffer_22
  assign controlled_buffer_20_out = rom_1_data[1] ? bit_extender_9_out : 32'bz;  // Controlled_Buffer controlled_buffer_23
  assign controlled_buffer_20_out = rom_1_data[0] ? bit_extender_10_out : 32'bz;  // Controlled_Buffer controlled_buffer_24

  // Notes on the sheet:
  //   contents of rom_1 (hex, n*v repeats v):
  //   1 2 4 8 10 20 40 80
  //   imm[31:12] / imm[20|10:1|11|19:12]
  //   AND
  //   OR
  //   SRL/SRA
  //   XOR
  //   SLTU
  //   SLT
  //   SLL
  //   ADD/SUB
  //   imm[11:0]
  //   shamt
  //   imm[4:0] / imm[4:1|11]
  //   imm[11:5] / imm[12|10:5]
  //   ANDI
  //   ORI
  //   SRLI/SRAI
  //   XORI
  //   SLTIU
  //   SLTI
  //   SLLI
  //   ADDI
  //   LHU
  //   LBU
  //   LW
  //   LH
  //   LB
endmodule

module main (
);

  wire clock_1_out;
  wire [4:0] rom_1_data_2, rom_1_data_4, rom_1_data_5;
  wire [6:0] rom_1_data;
  wire [23:0] counter_1_q, undriven;
  wire [24:5] rom_1_data_3;
  wire [31:0] alu_1_alu_out, register_file_1_rs1, register_file_1_rs2;

  Clock clock_1 (.out(clock_1_out));
  Counter #(.max('hffffff), .width(24)) counter_1 (
    .clk(clock_1_out), .Q(counter_1_q));  // open: clr, load, up, count, D, carry
  ROM #(.addrWidth(24), .dataWidth(32)) rom_1 (
    .addr(counter_1_q),
    .data({rom_1_data_3[24:18], rom_1_data_5, rom_1_data_4, rom_1_data_3[7:5], rom_1_data_2, rom_1_data}));
  register_file register_file_1 (
    .rd_in(rom_1_data_2), .clock(clock_1_out), .data_in(alu_1_alu_out), .rs1_in(rom_1_data_4),
    .rs2_in(rom_1_data_5), .rs1(register_file_1_rs1), .rs2(register_file_1_rs2));  // open: clear
  RAM #(.addrWidth(24), .dataWidth(32)) ram_1 (.addr(undriven));  // open: we, oe, clk, din, dout
  alu alu_1 (
    .rs2(register_file_1_rs2), .rs1(register_file_1_rs1), .funct7(rom_1_data_3[24:18]),
    .imm({rom_1_data_3[24:18], rom_1_data_5, rom_1_data_4, rom_1_data_3[7:5], rom_1_data_2}),
    .opcode(rom_1_data), .ram(undriven), .funct3(rom_1_data_3[7:5]), .alu_out(alu_1_alu_out));

  // Notes on the sheet:
  //   contents of rom_1 (hex, n*v repeats v):
  //   40208233
  //   funct7
  //   rs2
  //   rs1
  //   funct3
  //   rd
  //   opcode
  //   imm
endmodule
